# Fritzing sketch ESP32-Scanner (saved by Fritzing 0.9.3b)
perfboards: 1

parts:
  U1 = ESP32-38PinWide [part_number=ESP32-38PinWide]
  J1 = 2.1mm Barrel Jack with Terminal Block
  J2 = female pin header, 19 pins [form="♀ (female)"]
  J3 = female pin header, 19 pins [form="♀ (female)"]  # not connected
  S1 = Pushbutton [package="[THT]"]
  R1 = Resistor [tolerance=±5% resistance=10k package=THT]
  LED1 = LED - 5mm [color="Yellow (585nm)" package="5 mm [THT]"]
  LED2 = LED - 5mm [color="Green (570nm)" package="5 mm [THT]"]
  LED3 = LED - 5mm [color="Blue (505nm)" package="5 mm [THT]"]
  R2 = Resistor [tolerance=±5% resistance=220 package=THT]
  R3 = Resistor [tolerance=±5% resistance=220 package=THT]
  R4 = Resistor [tolerance=±5% resistance=220 package=THT]

nets:
  N1: U1.GPIO26, S1.Pin_3, S1.Pin_4, R1.Pin_0
  N2: J1.NEG, J2.pin2, R1.Pin_1, LED1.cathode, LED2.cathode, R2.Pin_1, R3.Pin_1, R4.Pin_1
  N3: J1.POS, J2.pin1
  N4: J2.pin7, LED3.anode
  N5: J2.pin8, LED2.anode
  N6: J2.pin9, LED1.anode
  N7: J2.pin19, S1.Pin_1, S1.Pin_2

custom parts:
  ESP32-38PinWide: Generic 38-Pin ESP32 with wide format (only access to one side of pins on a breadboard) based on Stephen Lilley's HiLetgo ESP-WROOM-32 ESP32 ESP-32S Development Board.
