# Fritzing sketch ESP8266-NoLevelConverter (saved by Fritzing 0.9.3b)
perfboards: 1

parts:
  J1 = 2.1mm Barrel Jack with Terminal Block
  Part1 = 24 NeoPixel Ring [part_number=1586]
  J3 = female pin header, 2 pins [form="♀ (female)"]
  J4 = female pin header, 2 pins [form="♀ (female)"]
  J5 = female pin header, 2 pins [form="♀ (female)"]
  U1 = ESP8266 NodeMCU LoLin module
  J6 = female pin header, 2 pins [form="♀ (female)"]
  C1 = Electrolytic Capacitor [capacitance=0.1mF voltage=35V package="100 mil [THT, electrolytic]"]  # not connected
  R1 = Resistor [tolerance=±5% resistance=470 package=THT]
  S1 = Pushbutton [package="[THT]"]
  R2 = Resistor [tolerance=±5% resistance=10k package=THT]
  LED1 = LED - 5mm [color="Red (633nm)" package="5 mm [THT]"]
  R3 = Resistor [tolerance=±5% resistance=220 package=THT]

nets:
  N1: J1.NEG, J3.pin1
  N2: Part1.IN, R1.Pin_0
  N3: Part1.VDD, J4.pin2
  N4: Part1.GND, J4.pin1
  N5: J5.pin2, S1.Pin_2
  N6: U1.D2, LED1.anode
  N7: U1.GND, R2.Pin_1, R3.Pin_1
  N8: J6.pin1, S1.Pin_4
  N9: LED1.cathode, R3.Pin_0

notes:
  Floating DC Jack, will placed on 3D Print
  Floating NeoPixel

custom parts:
  24 NeoPixel Ring: 24 ultra bright smart LED NeoPixels are arranged in a circle with 2.6" (66mm) outer diameter. The rings are 'chainable' - connect the output pin of one to the input pin of another. Use only one microcontroller pin to control as many as you can chain together! Each LED is addressable as the driver chip is inside the LED. Each one has ~18mA constant current drive so the color will be very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
  ESP8266 NodeMCU LoLin module: ESP8266 based NodeMCU
