# Fritzing sketch ESP8266-WithLevelConverter (saved by Fritzing 0.9.3b)
perfboards: 1

parts:
  J1 = 2.1mm Barrel Jack with Terminal Block
  M1 = Humidity and Temperature Sensor DHT11
  Part1 = 24 NeoPixel Ring [part_number=1586]
  J3 = female pin header, 2 pins [form="♀ (female)"]
  J4 = female pin header, 2 pins [form="♀ (female)"]
  J5 = female pin header, 2 pins [form="♀ (female)"]
  U1 = ESP8266 NodeMCU LoLin module  # not connected
  J6 = female pin header, 2 pins [form="♀ (female)"]
  R1 = Resistor [tolerance=±5% power=0.25 resistance=4.7k package=THT]
  C1 = Electrolytic Capacitor [capacitance=0.1mF voltage=35V package="100 mil [THT, electrolytic]"]  # not connected
  LLC1 = Logic Level Converter [package="Breakout board"]
  R3 = Resistor [tolerance=±5% power=0.25 resistance=470 package=THT]

nets:
  N1: J1.POS, LLC1.HV
  N2: J1.NEG, J3.pin1, LLC1.H-GND
  N3: M1.Vcc, J5.pin2, R1.Pin_1
  N4: M1.Data, J6.pin2, R1.Pin_0
  N5: M1.GND, J5.pin1
  N6: Part1.IN, R3.Pin_1
  N7: Part1.VDD, J4.pin2
  N8: Part1.GND, J4.pin1
  N9: J6.pin1, LLC1.LV4

notes:
  Floating DC Jack, will placed on 3D Print
  Floating DHT11
  Floating NeoPixel
  LevelShifter - Will placed on bottom of the ESP8266 if possible.

custom parts:
  Humidity and Temperature Sensor DHT11: Digital relative humidity & temperature sensor DHT11
  24 NeoPixel Ring: 24 ultra bright smart LED NeoPixels are arranged in a circle with 2.6" (66mm) outer diameter. The rings are 'chainable' - connect the output pin of one to the input pin of another. Use only one microcontroller pin to control as many as you can chain together! Each LED is addressable as the driver chip is inside the LED. Each one has ~18mA constant current drive so the color will be very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
  ESP8266 NodeMCU LoLin module: ESP8266 based NodeMCU
  Logic Level Converter: 5V to/from 3.3V logic level converter
